# Fritzing sketch GameCube_Pendant_JOG_Adapter (saved by Fritzing 0.9.3b)

parts:
  Part1 = Arduino Mega 2560 (Rev3)
  Part2 = Logic Level Converter
  C2 = Electrolytic Capacitor [capacitance=100µF package="100 mil [THT, electrolytic]"]
  R2 = Resistor [tolerance=±5% resistance=1k package=THT]
  CNCUSB_MK1_Jog_header = shrouded pin header, 26 pins [form="♂ (shrouded male)"]
  Gamecube_Controller = longpad pin header, 6 pins [form="long pad"]
  R1 = Resistor [tolerance=±5% resistance=1k package=THT]

nets:
  N1: Part1.3V3, Part2.LV, R2.Pin_0, Gamecube_Controller.pin6
  N2: Part1.5V, Part2.HV
  GND: Part1.GND, Part2.GND, C2.-, CNCUSB_MK1_Jog_header.pin6, Gamecube_Controller.pin1
  N3: Part1.D2_PWM, R1.Pin_1
  N4: Part1.D7_PWM, Part2.TX2_HV
  N5: Part1.D22, CNCUSB_MK1_Jog_header.pin10
  N6: Part1.D23, CNCUSB_MK1_Jog_header.pin17
  N7: Part1.D24, CNCUSB_MK1_Jog_header.pin9
  N8: Part1.D25, CNCUSB_MK1_Jog_header.pin18
  N9: Part1.D26, CNCUSB_MK1_Jog_header.pin8
  N10: Part1.D27, CNCUSB_MK1_Jog_header.pin19
  N11: Part1.D28, CNCUSB_MK1_Jog_header.pin7
  N12: Part1.D29, CNCUSB_MK1_Jog_header.pin20
  N13: Part2.TX2_LV, R2.Pin_1, Gamecube_Controller.pin5
  N14: CNCUSB_MK1_Jog_header.pin22, R1.Pin_0

notes:
  GND
  GND (rumble)
  5V (rumble)
  DATA
  3.3V
